# Fritzing sketch theramin2 (saved by Fritzing 1.0.4)
breadboards: 1

parts:
  Part1 = Adafruit CAP1188 - 8-Key Capacitive Touch Sensor Breakout [part_number="Adafruit #1602"]
  Part2 = Arduino Uno (Rev3) - ICSP
  R1 = Resistor [tolerance=±5% power=0.25W resistance=100 package=THT]
  LED1 = LED - 5mm [color="Red (633nm)" current=0.030A package="5 mm [THT]"]
  R2 = Photocell (LDR) [power=0.25W dark_resistance_@0.01lx=300kΩ light_resistance_@100lx=400Ω luminance=10lx package=THT]
  R3 = Resistor [tolerance=±5% power=0.25W resistance=220 package=THT]  # not connected

nets:
  N1: Part1.SDA/MISO, Part2.A4/SDA
  N2: Part1.SCK, Part2.A5/SCL
  VIN: Part1.VIN, Part2.5V, LED1.anode, R2.pin_0
  GND: Part1.GND, Part2.GND
  N3: Part2.A1, R2.pin_1
  N4: R1.Pin_1, LED1.cathode

custom parts:
  Adafruit CAP1188 - 8-Key Capacitive Touch Sensor Breakout: Add lots of touch sensors to your next microcontroller project with this easy-to-use 8-channel capacitive touch sensor breakout board, starring the CAP1188. This chip can handle up to 8 individual touch pads, and has a very nice feature that makes it stand out for us: it will light up the 8 onboard LEDs when the matching touch sensor fires to help you debug your sensor setup. The CAP1188 has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
